# Fritzing sketch rgb_dbl_ch_4x_Arr_02 (saved by Fritzing 0.9.2b)
breadboards: 1

parts:
  C1 = Ceramic Capacitor [capacitance=100nF package="100 mil [THT, multilayer]"]
  Part1 = Arduino Uno (Rev3)
  S1 = Pushbutton [package="[THT]"]
  LED1 = RGB LED - (4 legs) [package="5 mm [THT]"]
  LED2 = LED - 5mm [color="Red (633nm)" package="5 mm [THT]"]
  C2 = Ceramic Capacitor [capacitance=100nF package="100 mil [THT, multilayer]"]
  LED3 = LED - 5mm [color="Green (560nm)" package="5 mm [THT]"]
  LED4 = LED - 5mm [color="Blue (470nm)" package="5 mm [THT]"]
  RE1 = Rotary Encoder [package=THT]
  R8 = Resistor [tolerance=±5% resistance=680 package=THT]
  R13 = Resistor [tolerance=±5% resistance=680 package=THT]
  R14 = Resistor [tolerance=±5% resistance=680 package=THT]
  R15 = Resistor [tolerance=±5% resistance=680 package=THT]
  R16 = Resistor [tolerance=±5% resistance=680 package=THT]
  R17 = Resistor [tolerance=±5% resistance=680 package=THT]
  R2 = Resistor [tolerance=±5% resistance=10k package=THT]
  R18 = Resistor [tolerance=±5% resistance=10k package=THT]
  R3 = Resistor [tolerance=±5% resistance=10k package=THT]
  R19 = Resistor [tolerance=±5% resistance=10k package=THT]
  R20 = Resistor [tolerance=±5% resistance=10k package=THT]

nets:
  N1: C1.0, Part1.D2, R19.Pin_1
  N2: C1.1, Part1.GND, C2.0, RE1.EncoderPinC, R8.Pin_1, R13.Pin_1, R14.Pin_1, R20.Pin_0
  N3: Part1.A0, LED2.anode
  N4: Part1.A1, LED3.anode
  N5: Part1.A2, LED4.anode
  N6: Part1.D9_PWM, R17.Pin_0
  N7: Part1.D10_PWM/SS, R16.Pin_0
  N8: Part1.D11_PWM/MOSI, R15.Pin_0
  N9: Part1.D3_PWM, C2.1, R3.Pin_0
  N10: Part1.D7, S1.Pin_3, S1.Pin_4
  N11: Part1.5V, S1.Pin_1, S1.Pin_2, LED1.common_anode, R2.Pin_0, R18.Pin_0, R20.Pin_1
  N12: LED1.red_cathode, R15.Pin_1
  N13: LED1.green_cathode, R16.Pin_1
  N14: LED1.blue_cathode, R17.Pin_1
  N15: LED2.cathode, R14.Pin_0
  N16: LED3.cathode, R13.Pin_0
  N17: LED4.cathode, R8.Pin_0
  N18: RE1.EncoderPinA, R2.Pin_1, R19.Pin_0
  N19: RE1.EncoderPinB, R18.Pin_1, R3.Pin_1

// code stored in the sketch: rgb_dbl_ch_4x_Arr_02.ino
// Hands-On Arduino:
// Dr. Robert Paz:
// BD4x rotary encoder detection - double channel interrupt method:
// using Array:
// rotary encoder controlling RGB led with push button mode selector:


// rotary encoder max/min pulse counts (if clamping is required):
// mechanical (switch) rotatry encoder - 24 pulses per rot x4 (quadrature):

#define QMAX 96       // limit quadrature maximum pulse count for cw rotation:
#define QMIN 0        // limit quadrature minimum pulse count for ccw rotation:

/*
// uncomment this line if using a Common Anode LED:
#define COMMON_ANODE
*/

// mode switching:
byte modeButton = 7;          // rgb mode selector button pin:
boolean lastButton = LOW;
boolean currentButton = LOW;
byte modeIndicator = 13;      // rgb mode button on/off indicator led pin:
byte stateLedR = 14;          // Red mode indicator led (A0) pin:
byte stateLedG = 15;          // Green mode indicator led (A1) pin:
byte stateLedB = 16;          // Blue mode indicator led (A2) pin:
byte modeState = 0;           // mode cycle - 0, 1, 2, 3:
boolean mode = false;         // present state of indicator led (on/off):

// RGB led:
// RED:
byte rLed = 9;                // red led pin (~ PWM):
int rLevel = 255;               // red led pwm level;
int rCount = 0;               // red counter:
// GREEN:
byte gLed = 10;               // green led pin (~ PWM):
int gLevel = 255;               // green led pwm level:
int gCount = 0;               // green count:
// BLUE:
byte bLed = 11;               // blue led pin (~ PWM):
int bLevel = 255;               // blue led pwm level:
int bCount = 0;               // blue count:

// timing:
#define SETTIME 1000000       // microseconds:
unsigned long timep, time, etime;

// interupt counter:
long count = 0;
byte state, statep, index;

// Quadrature Encoder Matrix (Array):
int QEM [16] = {0, -1, 0, 1, 1, 0, -1, 0, 0, 1, 0, -1, -1, 0, 1, 0};

boolean A, B;                 // interrupt read:


void setup () {

    pinMode (stateLedR, OUTPUT);
    pinMode (stateLedG, OUTPUT);
    pinMode (stateLedB, OUTPUT);
    pinMode (modeIndicator, OUTPUT);
    digitalWrite (modeIndicator, LOW);
    pinMode (rLed, OUTPUT);
    analogWrite (rLed, 255);
    pinMode (gLed, OUTPUT);
    analogWrite (gLed, 255);
    pinMode (bLed, OUTPUT);
    analogWrite (bLed, 255);
    pinMode (modeButton, INPUT);          // to encoder push-button:

    Serial.begin (9600);                  // start serial monitor:
    
    pinMode (2, INPUT);                   // connect Channel A to pin 2:
    pinMode (3, INPUT);                   // connect Channel B to pin 3:
    
    attachInterrupt (0, ABchange, CHANGE); // setup interrupts (pins 2 and 3):
    attachInterrupt (1, ABchange, CHANGE);
    
    timep = micros ();                    // set the initial time:
    
    B = digitalRead (2);                  // read initial values of pins 2 and 3:
    A = digitalRead (3);
    
    if ((A == HIGH) && (B == HIGH)) statep = 0; // set initail state values:
    if ((A == HIGH) && (B == LOW)) statep = 1;
    if ((A == LOW) && (B == LOW)) statep = 2;
    if ((A == LOW) && (B == HIGH)) statep = 3;

    delay (500);

    printModeState ();
}


void loop () {

    buttonPress ();
    modeLed ();
    setMonitor ();    // serial monitor feed-back:

}


void ABchange () {                         // Interrupt Service Routine - Achange:

    B = digitalRead (2);
    A = digitalRead (3);
    
    if ((A == HIGH) && (B == HIGH)) state = 0;  // determine current state value:
    if ((A == HIGH) && (B == LOW)) state = 1;
    if ((A == LOW) && (B == LOW)) state = 2;
    if ((A == LOW) && (B == HIGH)) state = 3;

  //QEM [16] = {0, -1, 0, 1, 1, 0, -1, 0, 0, 1, 0, -1, -1, 0, 1, 0};
    index = (4 * state) + statep;
    count = count + QEM [index];

    countClamp ();                        // clamp count to max/min of quadrature of encoder:

    statep = state;                       // save current state:

}

/*
void Bchange () {                         // Interrupt Service Routine - Bchange:

    B = digitalRead (2);
    A = digitalRead (3);
    
    if ((A == HIGH) && (B == HIGH)) state = 0;  // determine current state value:
    if ((A == HIGH) && (B == LOW)) state = 1;
    if ((A == LOW) && (B == LOW)) state = 2;
    if ((A == LOW) && (B == HIGH)) state = 3;

  //QEM [16] = {0, -1, 0, 1, 1, 0, -1, 0, 0, 1, 0, -1, -1, 0, 1, 0};
    index = 4 * state + statep;
    count = count + QEM [index];

    countClamp ();                        // clamp count to max/min of quadrature of encoder:

    statep = state;

}
*/


void countClamp () {                      // clamp count from QMIN to QMAX:

    if (count > QMAX) {
        count = QMAX;
    }
    else if (count < QMIN) {
        count = QMIN;
    }

}


boolean debounce (boolean last) {         // mode button debounce:

    boolean current = digitalRead (modeButton);
    if (last != current) {
        delay (5);
        current = digitalRead (modeButton);
    }
    return current;

}


void printModeState () {
    Serial.print ("Mode: ");
    Serial.println (modeState);
}


void buttonPress () {
// if mode button is pressed (goes from 0 to 1) increment modeSate by 1
// when modeState is greater than 3, reset to 0:

    currentButton = debounce (lastButton);
    if (currentButton != lastButton) {
        if (currentButton == HIGH) {
            modeState ++;
            if (modeState > 3) {
                modeState = 0;
                printModeState ();
            }
            else {
                printModeState ();
            }
            mode = 1;
            digitalWrite (modeIndicator, mode);
        }
        else {
            mode = 0;
            digitalWrite (modeIndicator, mode);
        }
        
    }
    lastButton = currentButton;

}


void modeLed () {

    switch (modeState) {
        case 1:         // Red:
        {
            count = rCount;
            
            digitalWrite (stateLedR, HIGH);
            digitalWrite (stateLedG, LOW);
            digitalWrite (stateLedB, LOW);

            rLevel = map (count, QMIN, QMAX, 255, 0);
//            ifAnode ();
            analogWrite (rLed, rLevel);
            rCount = count;
            
            break;
        }
        case 2:         // Green:
        {
            count = gCount;
            
            digitalWrite (stateLedR, LOW);
            digitalWrite (stateLedG, HIGH);
            digitalWrite (stateLedB, LOW);

            gLevel = map (count, QMIN, QMAX, 255, 0);
//           ifAnode ();
            analogWrite (gLed, gLevel);
            gCount = count;
            
            break;
        }
        case 3:         // Blue:
        {
            count = bCount;
            
            digitalWrite (stateLedR, LOW);
            digitalWrite (stateLedG, LOW);
            digitalWrite (stateLedB, HIGH);

            bLevel = map (count, QMIN, QMAX, 255, 0);
//            ifAnode ();
            analogWrite (bLed, bLevel);
            bCount = count;
            
            break;
        }
        default:        // None:
        {
            digitalWrite (stateLedR, LOW);
            digitalWrite (stateLedG, LOW);
            digitalWrite (stateLedB, LOW);

            //count = count;
            
            break;
        }
    }

}


// Serial Monitor set-up feed-back and debugging:
void setMonitor () {                //    used only for serial monitor de-bugging:

    time = micros ();                     // set the current time:   
    etime = time - timep;                 // calculate elapsed time:
    if (etime > SETTIME) {                // test for time > 1 second:
        modeMonitor ();
        timep = time;                     // reset timer:
    }
}


void modeMonitor () {

    if (modeState == 1) {
        Serial.print ("Red mode selected: ");
        monitorPrint ();
    }
    else if (modeState == 2) {
        Serial.print ("Green mode selected: ");
        monitorPrint ();
    }
    else if (modeState == 3) {
        Serial.print ("Blue mode selected: ");
        monitorPrint ();
    }
    else {
        Serial.println ("No mode selected");
        monitorPrint ();
    }

}


void printRGBLevels () {
    Serial.print ("R:");
    Serial.print (255 - rLevel);
    Serial.print ("\tG:");
    Serial.print (255 - gLevel);
    Serial.print ("\tB:");
    Serial.println (255 - bLevel);
    Serial.println ();
}


void monitorPrint () {

    if (modeState > 0) {
        Serial.println (count);
        printRGBLevels ();
    }
    else {
        printRGBLevels ();
    }
     
}



/*
void ifAnode () {
    #ifdef COMMON_ANODE
          rLevel = 255 - rLevel;
          gLevel = 255 - gLevel;
          bLevel = 255 - bLevel;
    #endif
}
*/
